// Logisim project cpu.circ as structural Verilog: 1 circuit, main circuit CPU
module CPU (
  input  [31:0] Instruction,
  input  CLK,
  output [31:0] s0,
  output [31:0] s1,
  output [31:0] t0,
  output [31:0] t1,
  output [31:0] a0,
  output [31:0] ra,
  output [31:0] sp,
  output [31:0] PC
);

  wire main_1_p1, main_1_p2, main_1_p7, PC_normal, Sele2, SeleA, WE;
  wire [3:0] undriven;
  wire [4:0] RD, RS1, RS2;
  wire [31:0] A, alu_1_out, B, Imm, multiplexer_1_out, PC___4, PC_t, R1, R2, Resul, W;

  // Incrementer incrementer_1: pin names not known; wires that end beside it: PC, PC___4
  Multiplexer #(.width(32), .enable("false")) multiplexer_1 (
    .in0(Resul), .in1(PC___4), .out(multiplexer_1_out), .sel(PC_normal));
  // PC pc_1: pin names not known; wires that end beside it: multiplexer_1_out, CLK, PC
  RegFile regfile_1 (
    .Clk(CLK), .R1(R1), .R2(R2), .WE(WE), .W(W), .RD(RD), .RS1(RS1), .RS2(RS2), .s0(s0), .s1(s1), .t0(t0),
    .t1(t1), .a0(a0), .ra(ra), .sp(sp));
  Multiplexer #(.width(32), .enable("false")) multiplexer_2 (.in0(PC_t), .in1(R1), .out(A), .sel(SeleA));
  Multiplexer #(.width(32), .enable("false")) multiplexer_3 (.in0(Imm), .in1(R2), .out(B), .sel(Sele2));
  ALU alu_1 (.A(A), .B(B), .ALU_Op(undriven), .Out(alu_1_out));
  // memory_main main_1: pin names not known; wires that end beside it: main_1_p1, main_1_p2, alu_1_out, main_1_p1, main_1_p2, CLK, main_1_p7, main_1_p7, alu_1_out

  // Other names for the same wires on the sheet: fetch_addr[31:0] = PC; INST[31:0] = Instruction

  // Notes on the sheet:
  //   NOTE
  //   Please do not modify/replace/move/change/delete/etc input and output pins
  //   These are debug/test outputs from your circuit
endmodule
