// Logisim project regfile.circ as structural Verilog: 1 circuit, main circuit RegFile
module RegFile (
  input  [4:0] RD,
  input  [4:0] RS1,
  input  [4:0] RS2,
  input  [31:0] W,
  input  WE,
  input  Clk,
  output [31:0] s0,
  output [31:0] s1,
  output [31:0] t0,
  output [31:0] t1,
  output [31:0] a0,
  output [31:0] ra,
  output [31:0] sp,
  output [31:0] R1,
  output [31:0] R2
);

  wire and_6_out, and_7_out, Clk_t, decoder_1_out1, decoder_1_out3, decoder_1_out5, decoder_1_out7,
       decoder_1_out9, decoder_1_out11, decoder_1_out17;
  wire [31:1] GROUND;

  Decoder #(.select(5)) decoder_1 (
    .out1(decoder_1_out1), .out3(decoder_1_out3), .out5(decoder_1_out5), .out7(decoder_1_out7),
    .out9(decoder_1_out9), .out11(decoder_1_out11), .out17(decoder_1_out17), .en(RD[0]));  // open: out0, out2, out4, out6, out8, out10, out12, out13, out14, out15, out16, out18, out19, out20, out21, out22, out23, out24, out25, out26, out27, out28, out29, out30, out31, sel
  // AND_Gate and_1 has open pins: in0=WE, in4=decoder_1_out1, out=open
  // AND_Gate and_2 has open pins: in0=WE, in4=decoder_1_out17, out=open
  // AND_Gate and_3 has open pins: in0=WE, in4=decoder_1_out3, out=open
  // AND_Gate and_4 has open pins: in0=WE, in4=decoder_1_out5, out=open
  // AND_Gate and_5 has open pins: in0=WE, in4=decoder_1_out7, out=open
  and and_6 (and_6_out, WE, decoder_1_out9);
  and and_7 (and_7_out, WE, decoder_1_out11);
  Register #(.width(32)) Zero (.D({GROUND, 1'b0}), .clk(Clk_t));  // open: en, Q, clr
  Register #(.width(32)) u_ra (.D(W), .clk(Clk_t));  // open: en, Q, clr
  Register #(.width(32)) u_sp (.D(W), .clk(Clk_t));  // open: en, Q, clr
  Register #(.width(32)) u_t0 (.D(W), .clk(Clk_t));  // open: en, Q, clr
  Register #(.width(32)) u_t1 (.D(W), .clk(Clk_t));  // open: en, Q, clr
  Register #(.width(32)) u_s0 (.D(W), .clk(Clk_t));  // open: en, Q, clr
  Register #(.width(32)) u_s1 (.D(W), .clk(Clk_t));  // open: en, Q, clr
  Register #(.width(32)) u_a0 (.D(W), .en(and_6_out), .clk(Clk_t));  // open: Q, clr
  Register #(.width(32)) a1 (.D(W), .en(and_7_out), .clk(Clk_t));  // open: Q, clr
  Multiplexer #(.select(5)) multiplexer_1 ();  // open: in0, in1, in2, in3, in4, in5, in6, in7, in8, in9, in10, in11, in12, in13, in14, in15, in16, in17, in18, in19, in20, in21, in22, in23, in24, in25, in26, in27, in28, in29, in30, in31, out, sel, en
  Multiplexer #(.select(5)) multiplexer_2 ();  // open: in0, in1, in2, in3, in4, in5, in6, in7, in8, in9, in10, in11, in12, in13, in14, in15, in16, in17, in18, in19, in20, in21, in22, in23, in24, in25, in26, in27, in28, in29, in30, in31, out, sel, en
  // Pins of 1 and 32 bits meet at W
  // Pins of 1 and 5 bits meet at RD
  // Pins of 1 and 32 bits meet at {GROUND, 1'b0}

  // Notes on the sheet:
  //   Write Register
  //   Read Register 1
  //   Read Register 2
  //   Write Data
  //   Write Enable
  //   Clock
  //   NOTE
  //   Please do not modify/replace/move/change/delete/etc input and output pins
  //   These are debug/test outputs from your circuit
  //   Read Data 1
  //   Read Data 2
endmodule
